# Fritzing sketch AquaSlim (saved by Fritzing 0.9.5d)

parts:
  Mod1 = KY-019 5V Relay Module [package="Breakout board"]
  CPU1 = NodeMCU WROOM ESP 32
  M1 = fc-51 [package=THT]
  LED1 = LED - 5mm [color="Red (633nm)" package="5 mm [THT]"]

nets:
  N1: Mod1.S, CPU1.pin_10
  N2: Mod1.+, CPU1.pin_17, M1.pin3
  N3: Mod1.-, CPU1.pin_18, M1.pin2
  N4: Mod1.Common, LED1.cathode
  N5: Mod1.NO, LED1.anode
  N6: CPU1.pin_5, M1.pin1

custom parts:
  KY-019 5V Relay Module: KY-019 5V Relay module, used to control AC circuits. (Special thanks to vanepp for fixing the PCB holes and other errors)
  NodeMCU WROOM ESP 32: 30 pol Development Kit
